// Logisim project parte_b.circ as structural Verilog: 7 circuits, main circuit latch_rs
module latch_rs (
  input  in_1,
  input  in_2,
  output out_3,
  output out_4
);

  nor nor_1 (out_3, in_2, out_4);
  nor nor_2 (out_4, out_3, in_1);
endmodule

module latch_jk (
  input  in_1,
  input  in_2,
  output out_3,
  output out_4
);

  wire and_1_out, and_2_out;

  and and_1 (and_1_out, out_4, in_1);
  and and_2 (and_2_out, in_2, out_3);
  nor nor_1 (out_3, and_2_out, out_4);
  nor nor_2 (out_4, out_3, and_1_out);
endmodule

module latch_d (
  input  in_1,
  input  in_2,
  output out_3,
  output out_4
);

  wire and_1_out, and_2_out, not_1_out;

  not not_1 (not_1_out, in_1);
  and and_1 (and_1_out, in_1, in_2);
  and and_2 (and_2_out, in_2, not_1_out);
  nor nor_1 (out_3, and_2_out, out_4);
  nor nor_2 (out_4, out_3, and_1_out);
endmodule

module ej_4_registro_simple (
  input  in_1,
  input  in_2,
  input  in_3,
  input  in_4,
  input  in_5,
  input  in_6,
  output out_7,
  output out_8,
  output out_9,
  output out_10
);

  wire and_1_out;

  Register #(.width(1)) register_1 (.D(in_1), .Q(out_7), .clk(and_1_out));  // open: en, clr
  and and_1 (and_1_out, in_5, in_6);
  Register #(.width(1)) register_2 (.D(in_3), .Q(out_9), .clk(and_1_out));  // open: en, clr
  Register #(.width(1)) register_3 (.D(in_2), .Q(out_8), .clk(and_1_out));  // open: en, clr
  Register #(.width(1)) register_4 (.D(in_4), .Q(out_10), .clk(and_1_out));  // open: en, clr
endmodule

module ej_5_registro_bidireccional (
  input  in_1,
  input  in_2,
  input  in_3,
  input  in_4,
  input  in_5,
  input  in_6,
  input  in_7
);

  wire and_1_out, controlled_buffer_2_out, controlled_buffer_4_out, register_1_q, register_2_q, register_3_q,
       register_4_q;

  Controlled_Buffer controlled_buffer_1 (.in(register_1_q), .en(in_5));  // open: out
  Register #(.width(1)) register_1 (.D(in_1), .Q(register_1_q), .clk(and_1_out));  // open: en, clr
  and and_1 (and_1_out, in_6, in_7);
  assign controlled_buffer_2_out = in_5 ? register_2_q : 1'bz;  // Controlled_Buffer controlled_buffer_2
  Register #(.width(1)) register_2 (.D(in_2), .Q(register_2_q), .clk(and_1_out));  // open: en, clr
  assign in_3 = in_5 ? register_3_q : 1'bz;  // Controlled_Buffer controlled_buffer_3
  Register #(.width(1)) register_3 (.D(in_3), .Q(register_3_q), .clk(and_1_out));  // open: en, clr
  assign controlled_buffer_4_out = in_5 ? register_4_q : 1'bz;  // Controlled_Buffer controlled_buffer_4
  Register #(.width(1)) register_4 (.D(in_4), .Q(register_4_q), .clk(and_1_out));  // open: en, clr
endmodule

module ej_6_extensor_de_signo (
  input  in_1,
  input  in_2,
  input  in_3,
  input  in_4,
  input  in_5,
  input  in_6,
  input  in_7,
  output out_8,
  output out_9,
  output out_10,
  output out_11
);

  wire and_1_out, and_2_out, register_1_q, register_2_q, register_3_q;

  Register #(.width(1)) register_1 (.D(in_1), .Q(register_1_q), .clk(and_1_out));  // open: en, clr
  and and_1 (and_1_out, in_5, in_6);
  or or_1 (out_8, register_1_q, and_2_out);
  Register #(.width(1)) register_2 (.D(in_2), .Q(register_2_q), .clk(and_1_out));  // open: en, clr
  Register #(.width(1)) register_3 (.D(in_3), .Q(register_3_q), .clk(and_1_out));  // open: en, clr
  or or_2 (out_9, register_2_q, and_2_out);
  Register #(.width(1)) register_4 (.D(in_4), .Q(out_11), .clk(and_1_out));  // open: en, clr
  and and_2 (and_2_out, register_3_q, in_7);
  or or_3 (out_10, register_3_q, and_2_out);
endmodule

module ej_7_desplazador (
  input  in_1,
  input  in_2,
  input  in_3,
  input  in_4,
  input  in_5,
  input  in_6,
  input  in_7,
  output out_8,
  output out_9,
  output out_10,
  output out_11
);

  wire and_1_out, and_2_out, and_3_out, and_4_out, and_5_out, and_6_out, and_7_out, nand_1_out, not_1_out,
       not_2_out, not_3_out, register_1_q, register_2_q, register_3_q, register_4_q;

  not not_1 (not_1_out, in_7);
  and and_1 (and_1_out, register_1_q, not_1_out);
  or or_1 (out_8, and_1_out, and_4_out);
  Register #(.width(1)) register_1 (.D(in_1), .Q(register_1_q), .clk(and_2_out));  // open: en, clr
  and and_2 (and_2_out, in_5, in_6);
  and and_3 (and_3_out, register_2_q, not_2_out);
  and and_4 (and_4_out, in_7, register_2_q);
  Register #(.width(1)) register_2 (.D(in_2), .Q(register_2_q), .clk(and_2_out));  // open: en, clr
  Register #(.width(1)) register_3 (.D(in_3), .Q(register_3_q), .clk(and_2_out));  // open: en, clr
  not not_2 (not_2_out, in_7);
  and and_5 (and_5_out, in_7, register_3_q);
  or or_2 (out_9, and_3_out, and_5_out);
  Register #(.width(1)) register_4 (.D(in_4), .Q(register_4_q), .clk(and_2_out));  // open: en, clr
  not not_3 (not_3_out, in_7);
  and and_6 (and_6_out, in_7, register_4_q);
  and and_7 (and_7_out, register_3_q, not_3_out);
  or or_3 (out_10, and_7_out, and_6_out);
  nand nand_1 (nand_1_out, in_7, 1'b1);
  and and_8 (out_11, register_4_q, nand_1_out);
endmodule
