// Logisim project ej_5_4.circ as structural Verilog: 1 circuit, main circuit main
module main (
  input  in_1,
  input  in_2,
  input  in_3,
  input  in_4,
  input  in_5,
  input  in_6,
  input  in_7,
  input  in_8,
  input  in_9,
  input  in_10,
  input  in_11,
  input  in_12,
  input  in_13,
  input  in_14,
  input  in_15,
  output out_16,
  output out_17,
  output out_18,
  output out_19,
  output out_20,
  output out_21,
  output out_22
);

  wire and_1_out, and_2_out, and_3_out, and_4_out, and_5_out, nor_1_out, not_1_out, not_2_out, not_3_out,
       not_4_out, not_5_out, not_7_out, not_8_out, not_9_out, or_1_out, or_2_out;

  not not_1 (not_1_out, in_1);
  not not_2 (not_2_out, in_2);
  and and_1 (and_1_out, in_4, in_5);
  not not_3 (not_3_out, in_7);
  not not_4 (not_4_out, in_9);
  not not_5 (not_5_out, in_10);
  nor nor_1 (nor_1_out, not_1_out, not_2_out);
  not not_6 (out_17, and_1_out);
  and and_2 (and_2_out, in_6, not_3_out);
  or or_1 (or_1_out, not_5_out, in_11);
  or or_2 (or_2_out, in_10, not_7_out);
  not not_7 (not_7_out, in_11);
  xor xor_1 (out_20, in_12, in_13);
  xor xor_2 (out_21, in_12, in_14);
  xor xor_3 (out_22, in_12, in_15);
  not not_8 (not_8_out, nor_1_out);
  and and_3 (and_3_out, in_7, in_8);
  and and_4 (and_4_out, not_4_out, or_1_out);
  not not_9 (not_9_out, in_3);
  and and_5 (and_5_out, or_2_out, in_9);
  nor nor_2 (out_16, not_8_out, not_9_out);
  or or_3 (out_18, and_2_out, and_3_out);
  or or_4 (out_19, and_4_out, and_5_out);
endmodule
