// Logisim project ej_6_7_8_9_10.circ as structural Verilog: 8 circuits, main circuit sumador_simple
module sumador_simple (
  input  in_1,
  input  in_2,
  output out_3,
  output out_4
);

  xor xor_1 (out_3, in_1, in_2);
  and and_1 (out_4, in_1, in_2);
endmodule

module invierte_logicamente_4_bits (
  input  in_1,
  input  in_2,
  input  in_3,
  input  in_4,
  input  in_5,
  output out_6,
  output out_7,
  output out_8,
  output out_9
);

  invierte_logicamente_1_bit invierte_logicamente_1_bit_1 (.in_1(in_1), .in_2(in_5), .out_3(out_6));
  invierte_logicamente_1_bit invierte_logicamente_1_bit_2 (.in_1(in_2), .in_2(in_5), .out_3(out_7));
  invierte_logicamente_1_bit invierte_logicamente_1_bit_3 (.in_1(in_3), .in_2(in_5), .out_3(out_8));
  invierte_logicamente_1_bit invierte_logicamente_1_bit_4 (.in_1(in_4), .in_2(in_5), .out_3(out_9));
endmodule

module invierte_logicamente_1_bit (
  input  in_1,
  input  in_2,
  output out_3
);

  xor xor_1 (out_3, in_1, in_2);
endmodule

module ej_7_inv_aditivo_complemento_2 (
  input  in_1,
  input  in_2,
  input  in_3,
  input  in_4,
  input  in_5,
  output out_6,
  output out_7,
  output out_8,
  output out_9,
  output out_10
);

  wire invierte_logicamente_4_bits_1_out_6, invierte_logicamente_4_bits_1_out_7,
       invierte_logicamente_4_bits_1_out_8, invierte_logicamente_4_bits_1_out_9, not_1_out, not_2_out,
       not_3_out, sumador_simple_1_out_4, sumador_simple_2_out_4, sumador_simple_4_out_4;

  invierte_logicamente_4_bits invierte_logicamente_4_bits_1 (
    .in_1(in_1), .in_2(in_2), .in_3(in_3), .in_4(in_5), .in_5(in_4),
    .out_6(invierte_logicamente_4_bits_1_out_6), .out_7(invierte_logicamente_4_bits_1_out_7),
    .out_8(invierte_logicamente_4_bits_1_out_8), .out_9(invierte_logicamente_4_bits_1_out_9));
  not not_1 (not_1_out, in_3);
  not not_2 (not_2_out, in_5);
  sumador_simple sumador_simple_1 (
    .in_1(invierte_logicamente_4_bits_1_out_9), .in_2(in_4), .out_3(out_9), .out_4(sumador_simple_1_out_4));
  not not_3 (not_3_out, in_2);
  sumador_simple sumador_simple_2 (
    .in_1(invierte_logicamente_4_bits_1_out_8), .in_2(sumador_simple_1_out_4), .out_3(out_8),
    .out_4(sumador_simple_2_out_4));
  and and_1 (out_10, not_3_out, not_1_out, not_2_out);
  sumador_simple sumador_simple_3 (
    .in_1(invierte_logicamente_4_bits_1_out_6), .in_2(sumador_simple_4_out_4), .out_3(out_6));  // open: out_4
  sumador_simple sumador_simple_4 (
    .in_1(invierte_logicamente_4_bits_1_out_7), .in_2(sumador_simple_2_out_4), .out_3(out_7),
    .out_4(sumador_simple_4_out_4));
endmodule

module ej_8_demultiplexor (
  input  in_1,
  input  in_2,
  input  in_3,
  output out_4,
  output out_5,
  output out_6,
  output out_7
);

  wire and_1_out, and_2_out, and_3_out, and_4_out, and_5_out, and_6_out, and_7_out, and_8_out, not_1_out,
       not_2_out;

  not not_1 (not_1_out, in_2);
  and and_1 (and_1_out, in_2, in_3);
  and and_2 (and_2_out, not_1_out, not_2_out);
  not not_2 (not_2_out, in_3);
  and and_3 (and_3_out, in_1, and_1_out);
  and and_4 (and_4_out, not_1_out, in_3);
  and and_5 (and_5_out, in_2, not_2_out);
  or or_1 (out_7, and_3_out, 1'b0);
  and and_6 (and_6_out, in_1, and_2_out);
  and and_7 (and_7_out, in_1, and_4_out);
  and and_8 (and_8_out, in_1, and_5_out);
  or or_2 (out_4, and_6_out, 1'b0);
  or or_3 (out_5, and_7_out, 1'b0);
  or or_4 (out_6, and_8_out, 1'b0);
endmodule

module ej_9_codificador (
  input  in_1,
  input  in_2,
  input  in_3,
  input  in_4,
  output out_5,
  output out_6,
  output out_7
);

  wire xor_1_out;

  ExactlyOne xor_1 (.out(xor_1_out), .in0(in_4), .in1(in_3), .in2(in_2), .in3(in_1));
  not not_1 (out_7, xor_1_out);
  or or_1 (out_5, in_2, in_4);
  or or_2 (out_6, in_3, in_4);
endmodule

module ej_10_decodificador (
  input  in_1,
  input  in_2,
  output out_3,
  output out_4,
  output out_5,
  output out_6
);

  wire not_1_out, not_2_out, not_3_out, not_4_out;

  not not_1 (not_1_out, in_1);
  not not_2 (not_2_out, in_2);
  not not_3 (not_3_out, in_2);
  not not_4 (not_4_out, in_1);
  and and_1 (out_3, not_1_out, not_2_out);
  and and_2 (out_4, in_1, not_3_out);
  and and_3 (out_5, not_4_out, in_2);
  and and_4 (out_6, in_1, in_2);
endmodule

module ej_10b_demultiplexor_b (
  input  in_1,
  input  in_2,
  input  in_3,
  output out_4,
  output out_5,
  output out_6,
  output out_7
);

  wire and_1_out, and_2_out, and_3_out, and_4_out, ej_10_decodificador_1_out_3, ej_10_decodificador_1_out_4,
       ej_10_decodificador_1_out_5, ej_10_decodificador_1_out_6;

  ej_10_decodificador ej_10_decodificador_1 (
    .in_1(in_2), .in_2(in_3), .out_3(ej_10_decodificador_1_out_3), .out_4(ej_10_decodificador_1_out_4),
    .out_5(ej_10_decodificador_1_out_5), .out_6(ej_10_decodificador_1_out_6));
  and and_1 (and_1_out, in_1, ej_10_decodificador_1_out_3);
  and and_2 (and_2_out, in_1, ej_10_decodificador_1_out_4);
  and and_3 (and_3_out, in_1, ej_10_decodificador_1_out_5);
  and and_4 (and_4_out, in_1, ej_10_decodificador_1_out_6);
  or or_1 (out_4, and_1_out, 1'b0);
  or or_2 (out_5, and_2_out, 1'b0);
  or or_3 (out_6, and_3_out, 1'b0);
  or or_4 (out_7, and_4_out, 1'b0);
endmodule
